// Logisim project Elevator mini.circ as structural Verilog: 2 circuits, main circuit main
module main (
  input  GROUND,
  input  _1_st_floor,
  input  _2nd_floor,
  input  _3rd_floor,
  input  GROUND_2,
  input  _1st_floor,
  input  _2nd_floor_2,
  input  _3rd_floor_2,
  output out_9,
  output out_10
);

  wire clock_1_out, comparator_1_eq, comparator_1_gt, comparator_1_lt, n4bit_decoder_1_a_2,
       n4bit_decoder_1_b_2, n4bit_decoder_1_c, n4bit_decoder_1_d, n4bit_decoder_1_e, n4bit_decoder_1_f,
       n4bit_decoder_1_g, n4bit_decoder_2_a_2, n4bit_decoder_2_b_2, n4bit_decoder_2_c, n4bit_decoder_2_d,
       n4bit_decoder_2_e, n4bit_decoder_2_f, n4bit_decoder_2_g;
  wire [1:0] d_ff_1_q, d_ff_3_q, priority_encoder_1_out, priority_encoder_2_out;

  Priority_Encoder #(.select(2)) priority_encoder_1 (
    .in0(GROUND), .in1(_1_st_floor), .in2(_2nd_floor), .in3(_3rd_floor), .out(priority_encoder_1_out),
    .gs(out_9));  // open: en_out, en_in
  Priority_Encoder #(.select(2)) priority_encoder_2 (
    .in0(GROUND_2), .in1(_1st_floor), .in2(_2nd_floor_2), .in3(_3rd_floor_2), .out(priority_encoder_2_out),
    .gs(out_10));  // open: en_out, en_in
  _4bit_decoder u_4bit_decoder_1 (
    .B(priority_encoder_1_out[1]), .A(priority_encoder_1_out[0]), .a_2(n4bit_decoder_1_a_2),
    .b_2(n4bit_decoder_1_b_2), .c(n4bit_decoder_1_c), .d(n4bit_decoder_1_d), .e(n4bit_decoder_1_e),
    .f(n4bit_decoder_1_f), .g(n4bit_decoder_1_g));
  _7_Segment_Display u_7_segment_display_1 (
    .g(n4bit_decoder_1_g), .f(n4bit_decoder_1_f), .a(n4bit_decoder_1_a_2), .b(n4bit_decoder_1_b_2),
    .e(n4bit_decoder_1_e), .d(n4bit_decoder_1_d), .c(n4bit_decoder_1_c));  // open: dp
  _4bit_decoder u_4bit_decoder_2 (
    .B(priority_encoder_2_out[1]), .A(priority_encoder_2_out[0]), .a_2(n4bit_decoder_2_a_2),
    .b_2(n4bit_decoder_2_b_2), .c(n4bit_decoder_2_c), .d(n4bit_decoder_2_d), .e(n4bit_decoder_2_e),
    .f(n4bit_decoder_2_f), .g(n4bit_decoder_2_g));
  _7_Segment_Display u_7_segment_display_2 (
    .g(n4bit_decoder_2_g), .f(n4bit_decoder_2_f), .a(n4bit_decoder_2_a_2), .b(n4bit_decoder_2_b_2),
    .e(n4bit_decoder_2_e), .d(n4bit_decoder_2_d), .c(n4bit_decoder_2_c));  // open: dp
  Clock clock_1 (.out(clock_1_out));
  D_Flip_Flop d_ff_1 (
    .clk(clock_1_out), .D(priority_encoder_1_out[0]), .Q(d_ff_1_q[0]));  // open: Qn, preset, en, reset
  D_Flip_Flop d_ff_2 (
    .clk(clock_1_out), .D(priority_encoder_1_out[1]), .Q(d_ff_1_q[1]));  // open: Qn, preset, en, reset
  D_Flip_Flop d_ff_3 (
    .clk(clock_1_out), .D(priority_encoder_2_out[0]), .Q(d_ff_3_q[0]));  // open: Qn, preset, en, reset
  D_Flip_Flop d_ff_4 (
    .clk(clock_1_out), .D(priority_encoder_2_out[1]), .Q(d_ff_3_q[1]));  // open: Qn, preset, en, reset
  Comparator #(.width(2), .mode("unsigned")) comparator_1 (
    .a(d_ff_1_q), .b(d_ff_3_q), .gt(comparator_1_gt), .eq(comparator_1_eq), .lt(comparator_1_lt));
  LED UP (.in(comparator_1_gt));
  LED STOP (.in(comparator_1_eq));
  LED DOWN (.in(comparator_1_lt));

  // Notes on the sheet:
  //   Next floor
  //   Present Floor
  //   NEXT Floor
  //   Present Floor
endmodule

module _4bit_decoder (
  input  B,
  input  A,
  output a_2,
  output b_2,
  output c,
  output d,
  output e,
  output f,
  output g
);

  wire not_1_out, not_2_out, not_3_out, not_5_out, not_6_out;

  not not_1 (not_1_out, A);
  not not_2 (not_2_out, B);
  not not_3 (not_3_out, A);
  not not_4 (e, A);
  not not_5 (not_5_out, B);
  not not_6 (not_6_out, A);
  or or_1 (a_2, not_1_out, B);
  or or_2 (c, not_2_out, A);
  or or_3 (d, not_3_out, B);
  and and_1 (f, not_5_out, not_6_out);

  assign b_2 = 1'b1;
  assign g = B;
endmodule
